# Fritzing sketch sketch (saved by Fritzing 0.9.3b)
breadboards: 1

parts:
  Mod1 = Raspberry Pi Pico W
  Potentiometer = Rotary Potentiometer (Large) [maximum_resistance=100kΩ package=THT]
  Red_LED = smd LED [color="Red (633nm)" package="1206 [SMD]"]
  part = Resistor [tolerance=±5% resistance=220 package=THT]
  Yellow_LED = smd LED [color="Red (633nm)" package="1206 [SMD]"]
  part_2 = Resistor [tolerance=±5% resistance=220 package=THT]
  Blue_LED = smd LED [color="Red (633nm)" package="1206 [SMD]"]
  part_3 = Resistor [tolerance=±5% resistance=220 package=THT]

nets (from the schematic view):
  N1: Mod1.pin_3, Mod1.pin_28, Mod1.pin_33, Mod1.pin_38, Potentiometer.wiper, part.Pin_0, part_2.Pin_0, part_3.Pin_0
  N2: Mod1.pin_21, Yellow_LED.anode
  N3: Mod1.pin_22, Blue_LED.anode
  N4: Mod1.pin_36, Potentiometer.leg2
  N5: Potentiometer.leg1, Red_LED.anode
  N6: Red_LED.cathode, part.Pin_1
  N7: Yellow_LED.cathode, part_2.Pin_1
  N8: Blue_LED.cathode, part_3.Pin_1

custom parts:
  Raspberry Pi Pico W: Raspberry Pi Pico W. Based around the RP2040 microcontroller the Pico W is a low cost microcontroller device bringing Raspberry Pi quality, cost, and easy of use to the microcontroller space. The areas marked KEEPOUT in pcb silkscreen should not have traces running through them to avoid shorts on a soldered in module!
